# Fritzing sketch New Design (saved by Fritzing 0.9.3b)
circuit board: 19.1112cm x 7.30456cm
breadboards: 1

parts:
  U1 = WS2812 RGB LED strip
  Part1 = Arduino Uno (Rev3)
  LCD1 = LCD screen
  LED1 = smd LED [color="Red (633nm)" package="0603 [SMD]"]
  LCM1602_IIC1 = LCM1602 IIC [part_number="LCM1602 IIC" chip_label="LCM1602 IIC" package="DIP (Dual Inline) [THT]"]
  S2 = Momentary Switch [package=ksa_sealed_tac_switch]
  S3 = Momentary Switch [package=ksa_sealed_tac_switch]
  S4 = Momentary Switch [package=ksa_sealed_tac_switch]
  S5 = Toggle Switch [package=THT]
  U2 = POT [package=pot_alpha_rv16af-20]
  U3 = POT [package=pot_alpha_rv16af-20]
  U4 = POT [package=pot_alpha_rv16af-20]
  U5 = POT [package=pot_alpha_rv16af-20]
  LED2 = smd LED [color="Red (633nm)" package="0603 [SMD]"]
  M1 = DC Motor
  LED3 = smd LED [color="Red (633nm)" package="0603 [SMD]"]
  LED4 = smd LED [color="Red (633nm)" package="0603 [SMD]"]
  hc-sr1 = hc-sr04
  T1 = TMP36 Temperature Sensor [package="TO92 [THT]"]

nets:
  GND: U1.GND, Part1.D9_PWM, Part1.GND, LED1.cathode, LED1.anode, LCM1602_IIC1.GND, S2.3, S3.3, S4.3, S5.L1, U2.A, U3.A, U4.A, U5.A, LED2.cathode, LED3.cathode, LED4.cathode, hc-sr1.GND, T1.GND
  VCC: U1.VCC, Part1.5V, LCM1602_IIC1.VCC, S5.L2, U2.E, U4.E, U5.E, hc-sr1.VCC, T1.+Vs
  N1: U1.DIN, Part1.D3_PWM
  N2: Part1.A0, U4.S
  N3: Part1.A1, U5.S
  N4: Part1.A2, U2.S
  N5: Part1.A3, T1.Vout
  N6: Part1.A4/SDA, LCM1602_IIC1.SDA
  N7: Part1.A5/SCL, LCM1602_IIC1.SCL
  N8: Part1.D8, S2.1
  N9: Part1.D10_PWM/SS, hc-sr1.Echo
  N10: Part1.D11_PWM/MOSI, hc-sr1.Trig
  N11: Part1.D12/MISO, S3.1
  N12: Part1.D13/SCK, LED2.anode
  N13: Part1.D2, S5.COM
  N14: Part1.D4, M1.pin_2
  N15: Part1.D5_PWM, LED3.anode
  N16: Part1.D6_PWM, LED4.anode
  N17: Part1.D7, M1.pin_1
  N18: Part1.RESET, S4.1
  VSS: LCD1.VSS, LCM1602_IIC1.VSS
  VDD: LCD1.VDD, LCM1602_IIC1.VDD
  N19: LCD1.V0, LCM1602_IIC1.V0
  N20: LCD1.RS, LCM1602_IIC1.RS
  N21: LCD1.R/W, LCM1602_IIC1.RW
  N22: LCD1.E, LCM1602_IIC1.E
  N23: LCD1.DB0, LCM1602_IIC1.D0
  N24: LCD1.DB1, LCM1602_IIC1.D1
  N25: LCD1.DB2, LCM1602_IIC1.D2
  N26: LCD1.DB3, LCM1602_IIC1.D3
  N27: LCD1.DB4, LCM1602_IIC1.D4
  N28: LCD1.DB5, LCM1602_IIC1.D5
  N29: LCD1.DB6, LCM1602_IIC1.D6
  N30: LCD1.DB7, LCM1602_IIC1.D7
  N31: LCD1.LED+, LCM1602_IIC1.A
  N32: LCD1.LED-, LCM1602_IIC1.K
  N33: LCM1602_IIC1.LED_A, U3.S
  N34: LCM1602_IIC1.LED_B, U3.E

custom parts:
  WS2812 RGB LED strip: WS2812 strip
  LCM1602 IIC: I2C-Module to use a 1602 or 2004 LCD on with the wire.h libory Serial LCD Modul
